// Logisim project contadorSicronoControlado3a0e0a3.circ as structural Verilog: 1 circuit, main circuit main
module main (
  input  in_1
);

  wire clock_1_out, clock_2_out, not_1_out, not_2_out, t_ff_1_q, t_ff_2_q, t_ff_3_q, t_ff_4_q;
  wire [1:0] or_1_out;

  not not_1 (not_1_out, in_1);
  not not_2 (not_2_out, in_1);
  T_Flip_Flop t_ff_1 (.T(in_1), .clk(clock_1_out), .Q(t_ff_1_q), .reset(not_1_out));  // open: Qn, preset
  Clock clock_1 (.out(clock_1_out));
  T_Flip_Flop #(.trigger("falling")) t_ff_2 (
    .T(not_2_out), .clk(clock_2_out), .Q(t_ff_2_q), .reset(in_1));  // open: Qn, preset
  Clock clock_2 (.out(clock_2_out));
  T_Flip_Flop t_ff_3 (.T(1'b1), .clk(t_ff_1_q), .Q(t_ff_3_q), .reset(not_1_out));  // open: Qn, preset
  T_Flip_Flop #(.trigger("falling")) t_ff_4 (.T(1'b1), .clk(t_ff_2_q), .Q(t_ff_4_q), .reset(in_1));  // open: Qn, preset
  or or_1 (or_1_out[0], t_ff_1_q, t_ff_2_q);
  or or_2 (or_1_out[1], t_ff_3_q, t_ff_4_q);
  Hex_Digit_Display hex_digit_display_1 (.value({2'b00, or_1_out}));  // open: dp
endmodule
