// Logisim project conversorCodigoGray.circ as structural Verilog: 9 circuits, main circuit main
module main (
);

  wire clock_1_out, j0_1_out_4, j1_1_out_4, j2_1_out_4, j3_1_out_4, k0_1_out_4, k1_1_out_4, k2_1_out_4,
       k3_1_out_4;
  wire [3:0] j_k_ff_1_q;

  J0 j0_1 (.out_4(j0_1_out_4), .Q1(j_k_ff_1_q[1]), .Q2(j_k_ff_1_q[2]), .Q3(j_k_ff_1_q[3]));
  K0 k0_1 (.out_4(k0_1_out_4), .Q1(j_k_ff_1_q[1]), .Q2(j_k_ff_1_q[2]), .Q3(j_k_ff_1_q[3]));
  J1 j1_1 (.out_4(j1_1_out_4), .Q3(j_k_ff_1_q[3]), .Q2(j_k_ff_1_q[2]), .Q0(j_k_ff_1_q[0]));
  K1 k1_1 (.out_4(k1_1_out_4), .Q3(j_k_ff_1_q[3]), .Q2(j_k_ff_1_q[2]), .Q0(j_k_ff_1_q[0]));
  J2 j2_1 (.out_4(j2_1_out_4), .Q0(j_k_ff_1_q[0]), .Q3(j_k_ff_1_q[3]), .Q1(j_k_ff_1_q[1]));
  K2 k2_1 (.out_4(k2_1_out_4), .Q0(j_k_ff_1_q[0]), .Q3(j_k_ff_1_q[3]), .Q1(j_k_ff_1_q[1]));
  J3 j3_1 (.out_4(j3_1_out_4), .Q2(j_k_ff_1_q[2]), .Q1(j_k_ff_1_q[1]), .Q0(j_k_ff_1_q[0]));
  K3 k3_1 (.out_4(k3_1_out_4), .Q2(j_k_ff_1_q[2]), .Q1(j_k_ff_1_q[1]), .Q0(j_k_ff_1_q[0]));
  Clock clock_1 (.out(clock_1_out));
  J_K_Flip_Flop j_k_ff_1 (
    .J(j0_1_out_4), .K(k0_1_out_4), .clk(clock_1_out), .Q(j_k_ff_1_q[0]));  // open: Qn, preset, reset
  J_K_Flip_Flop j_k_ff_2 (
    .J(j1_1_out_4), .K(k1_1_out_4), .clk(clock_1_out), .Q(j_k_ff_1_q[1]));  // open: Qn, preset, reset
  J_K_Flip_Flop j_k_ff_3 (
    .J(j2_1_out_4), .K(k2_1_out_4), .clk(clock_1_out), .Q(j_k_ff_1_q[2]));  // open: Qn, preset, reset
  J_K_Flip_Flop j_k_ff_4 (
    .J(j3_1_out_4), .K(k3_1_out_4), .clk(clock_1_out), .Q(j_k_ff_1_q[3]));  // open: Qn, preset, reset
  Hex_Digit_Display hex_digit_display_1 (.value(j_k_ff_1_q));  // open: dp
endmodule

module J0 (
  input  Q1,
  input  Q2,
  input  Q3,
  output out_4
);

  wire and_1_out, and_2_out, and_3_out, and_4_out;

  or or_1 (out_4, and_1_out, and_2_out, and_3_out, and_4_out);
  and and_1 (and_1_out, Q1, Q2, ~Q3);  // AND_Gate
  and and_2 (and_2_out, Q1, ~Q2, Q3);  // AND_Gate
  and and_3 (and_3_out, ~Q1, Q2, Q3);  // AND_Gate
  and and_4 (and_4_out, ~Q1, ~Q2, ~Q3);  // AND_Gate
endmodule

module K0 (
  input  Q1,
  input  Q2,
  input  Q3,
  output out_4
);

  wire and_1_out, and_2_out, and_3_out, and_4_out;

  or or_1 (out_4, and_1_out, and_2_out, and_3_out, and_4_out);
  and and_1 (and_1_out, Q1, ~Q2, ~Q3);  // AND_Gate
  and and_2 (and_2_out, Q1, Q2, Q3);
  and and_3 (and_3_out, ~Q1, ~Q2, Q3);  // AND_Gate
  and and_4 (and_4_out, ~Q1, ~Q3, Q2);  // AND_Gate
endmodule

module J1 (
  input  Q3,
  input  Q2,
  input  Q0,
  output out_4
);

  wire and_1_out, and_2_out;

  and and_1 (and_1_out, Q0, Q2, Q3);
  or or_1 (out_4, and_1_out, and_2_out);
  and and_2 (and_2_out, ~Q2, ~Q3, Q0);  // AND_Gate
endmodule

module K1 (
  input  Q3,
  input  Q2,
  input  Q0,
  output out_4
);

  wire and_1_out, and_2_out;

  and and_1 (and_1_out, Q0, ~Q2, Q3);  // AND_Gate
  or or_1 (out_4, and_1_out, and_2_out);
  and and_2 (and_2_out, Q2, ~Q3, Q0);  // AND_Gate
endmodule

module J2 (
  input  Q0,
  input  Q3,
  input  Q1,
  output out_4
);

  and and_1 (out_4, ~Q0, ~Q3, Q1);  // AND_Gate
endmodule

module K2 (
  input  Q0,
  input  Q3,
  input  Q1,
  output out_4
);

  and and_1 (out_4, ~Q0, Q3, Q1);  // AND_Gate
endmodule

module J3 (
  input  Q2,
  input  Q1,
  input  Q0,
  output out_4
);

  and and_1 (out_4, Q2, ~Q1, ~Q0);  // AND_Gate
endmodule

module K3 (
  input  Q2,
  input  Q1,
  input  Q0,
  output out_4
);

  and and_1 (out_4, ~Q2, ~Q1, ~Q0);  // AND_Gate
endmodule
