// Logisim project conversorDeNumeros.circ as structural Verilog: 3 circuits, main circuit main
module main (
  input  S3,
  input  S2,
  input  S1,
  input  S0
);

  wire descriptografador_1_d0, descriptografador_1_d1, descriptografador_1_d2, descriptografador_1_d3,
       descriptografador_1_d4, descriptografador_1_d5, descriptografador_1_d6;

  descriptografador descriptografador_1 (
    .D2(descriptografador_1_d2), .D1(descriptografador_1_d1), .D0(descriptografador_1_d0),
    .D5(descriptografador_1_d5), .D4(descriptografador_1_d4), .D3(descriptografador_1_d3),
    .D6(descriptografador_1_d6), .A3(S3), .A2(S2), .A1(S1), .A0(S0));
  _7_Segment_Display u_7_segment_display_1 (
    .g(descriptografador_1_d0), .f(descriptografador_1_d1), .a(descriptografador_1_d6),
    .b(descriptografador_1_d5), .e(descriptografador_1_d2), .d(descriptografador_1_d3),
    .c(descriptografador_1_d4), .dp(1'b0));
endmodule

module CONTADOR (
  input  S3,
  input  S2,
  input  S1,
  input  S0,
  output D6,
  output D5,
  output D4,
  output D3,
  output D2,
  output D1,
  output D0
);

  wire and_1_out, and_2_out, and_3_out, and_4_out, and_5_out, and_6_out, and_7_out, and_8_out, and_9_out,
       and_10_out, and_11_out, and_12_out, and_13_out, and_14_out, and_15_out, and_16_out, and_17_out,
       and_18_out, and_19_out, and_20_out, and_21_out, and_22_out, and_23_out, and_24_out, and_25_out,
       and_26_out;

  and and_1 (and_1_out, ~S3, S2);  // AND_Gate
  and and_2 (and_2_out, ~S2, ~S0);  // AND_Gate
  and and_3 (and_3_out, S2, ~S1, S3);  // AND_Gate
  and and_4 (and_4_out, ~S0, S1);  // AND_Gate
  and and_5 (and_5_out, ~S2, S1, S3);  // AND_Gate
  and and_6 (and_6_out, ~S3, S2, S0);  // AND_Gate
  and and_7 (and_7_out, S3, S2);
  and and_8 (and_8_out, ~S2, ~S3);  // AND_Gate
  and and_9 (and_9_out, S0, ~S1, S3);  // AND_Gate
  and and_10 (and_10_out, ~S0, S2, ~S1);  // AND_Gate
  and and_11 (and_11_out, S0, S1, S2);
  and and_12 (and_12_out, ~S2, S3);  // AND_Gate
  and and_13 (and_13_out, ~S1, S0);  // AND_Gate
  and and_14 (and_14_out, ~S3, S0);  // AND_Gate
  and and_15 (and_15_out, ~S3, ~S1);  // AND_Gate
  and and_16 (and_16_out, ~S1, S3);  // AND_Gate
  and and_17 (and_17_out, ~S0, ~S2, ~S3);  // AND_Gate
  and and_18 (and_18_out, S0, S2, ~S3);  // AND_Gate
  and and_19 (and_19_out, S2, ~S0, S3, S1);  // AND_Gate
  and and_20 (and_20_out, ~S0, ~S2);  // AND_Gate
  and and_21 (and_21_out, ~S0, ~S1);  // AND_Gate
  and and_22 (and_22_out, S1, S3);
  and and_23 (and_23_out, S1, ~S0, S2);  // AND_Gate
  and and_24 (and_24_out, S2, ~S1, ~S3);  // AND_Gate
  and and_25 (and_25_out, S0, S3);
  and and_26 (and_26_out, S1, ~S2, ~S3);  // AND_Gate
  or or_1 (D5, and_7_out, and_8_out, and_9_out, and_10_out, and_11_out);
  or or_2 (D4, and_12_out, and_1_out, and_13_out, and_14_out, and_15_out);
  or or_3 (D3, and_16_out, and_17_out, and_18_out, and_19_out);
  or or_4 (D2, and_20_out, and_4_out, and_7_out, and_5_out);
  or or_5 (D1, and_21_out, and_12_out, and_22_out, and_23_out, and_24_out);
  or or_6 (D0, and_12_out, and_4_out, and_25_out, and_24_out, and_26_out);
  or or_7 (D6, and_1_out, and_2_out, and_3_out, and_4_out, and_5_out, and_6_out);
endmodule

module descriptografador (
  input  A3,
  input  A2,
  input  A1,
  input  A0,
  output D6,
  output D5,
  output D4,
  output D3,
  output D2,
  output D1,
  output D0
);

  wire and_1_out, and_2_out, and_3_out, and_4_out, and_5_out, and_6_out, and_7_out, and_8_out, and_9_out,
       and_10_out, and_11_out, and_12_out, and_13_out, and_14_out, and_15_out, and_16_out, and_17_out,
       and_18_out, and_19_out, and_20_out, and_21_out, and_22_out, and_23_out, and_24_out, and_25_out,
       and_26_out, and_27_out, and_28_out, and_29_out, and_30_out;

  and and_1 (and_1_out, ~A3, A1);  // AND_Gate
  and and_2 (and_2_out, ~A0, A1);  // AND_Gate
  and and_3 (and_3_out, A1, A2);
  and and_4 (and_4_out, ~A0, A3);  // AND_Gate
  and and_5 (and_5_out, ~A0, ~A2);  // AND_Gate
  and and_6 (and_6_out, A2, A0, ~A3);  // AND_Gate
  and and_7 (and_7_out, ~A1, ~A2, A3);  // AND_Gate
  and and_8 (and_8_out, ~A3, ~A2);  // AND_Gate
  and and_9 (and_9_out, ~A0, ~A1, ~A3);  // AND_Gate
  and and_10 (and_10_out, A0, A3, ~A1);  // AND_Gate
  and and_11 (and_11_out, A0, A1, ~A3);  // AND_Gate
  and and_12 (and_12_out, A3, ~A2);  // AND_Gate
  and and_13 (and_13_out, A0, ~A1);  // AND_Gate
  and and_14 (and_14_out, ~A1, ~A3);  // AND_Gate
  and and_15 (and_15_out, A0, ~A3);  // AND_Gate
  and and_16 (and_16_out, A2, ~A3);  // AND_Gate
  and and_17 (and_17_out, A3, ~A1);  // AND_Gate
  and and_18 (and_18_out, ~A0, ~A2, ~A3);  // AND_Gate
  and and_19 (and_19_out, A0, A2, ~A1);  // AND_Gate
  and and_20 (and_20_out, A2, A1, ~A0);  // AND_Gate
  and and_21 (and_21_out, A0, A1, ~A2);  // AND_Gate
  and and_22 (and_22_out, A2, A3);
  and and_23 (and_23_out, ~A0, ~A2);  // AND_Gate
  and and_24 (and_24_out, ~A0, ~A1);  // AND_Gate
  and and_25 (and_25_out, A1, A3);
  and and_26 (and_26_out, ~A1, A2, ~A3);  // AND_Gate
  and and_27 (and_27_out, ~A0, A2);  // AND_Gate
  and and_28 (and_28_out, A0, A3);
  and and_29 (and_29_out, ~A2, A1, ~A3);  // AND_Gate
  and and_30 (and_30_out, A3, ~A2);  // AND_Gate
  or or_1 (D6, and_1_out, and_2_out, and_3_out, and_4_out, and_5_out, and_6_out, and_7_out);
  or or_2 (D5, and_8_out, and_5_out, and_9_out, and_10_out, and_11_out);
  or or_3 (D4, and_12_out, and_13_out, and_14_out, and_15_out, and_16_out);
  or or_4 (D3, and_17_out, and_18_out, and_19_out, and_20_out, and_21_out);
  or or_5 (D2, and_22_out, and_2_out, and_23_out, and_25_out);
  or or_6 (D1, and_30_out, and_24_out, and_25_out, and_26_out, and_27_out);
  or or_7 (D0, and_30_out, and_2_out, and_28_out, and_26_out, and_29_out);

  // Notes on the sheet:
  //   D
  //   G
  //   A
  //   B
  //   C
  //   E
  //   F
endmodule
