// Logisim project praticaCofre.circ as structural Verilog: 4 circuits, main circuit main
module main (
);

  wire and_1_out, and_2_out, and_3_out, and_4_out, and_5_out, and_6_out, and_7_out, and_8_out, and_9_out,
       and_10_out, and_11_out, and_12_out, d_ff_1_q, d_ff_2_q, d_ff_3_q, d_ff_4_q, ENTER_out, I1_out, I2_out,
       I3_out, I4_out, I5_out, I6_out, I7_out, I8_out, I9_out, j_k_ff_1_q, j_k_ff_2_q, j_k_ff_3_q,
       j_k_ff_4_q, j_k_ff_5_q, or_1_out, or_2_out, or_3_out, or_4_out, or_5_out, or_6_out, or_7_out,
       or_8_out, or_9_out, RESTART_out, teclado_1_out_12, teclado_1_out_13, teclado_1_out_14,
       teclado_1_out_15, teclado_1_out_16, teclado_1_out_17, teclado_1_out_18;

  Button I9 (.out(I9_out));
  Button I8 (.out(I8_out));
  Button I7 (.out(I7_out));
  Button I6 (.out(I6_out));
  Button I5 (.out(I5_out));
  Button I4 (.out(I4_out));
  Button I3 (.out(I3_out));
  Button I2 (.out(I2_out));
  Button I1 (.out(I1_out));
  Button ENTER (.out(ENTER_out));
  Button RESTART (.out(RESTART_out));
  segredo2 segredo2_1 (
    ._9(I9_out), ._8(I8_out), ._7(I7_out), ._6(I6_out), ._5(I5_out), ._4(I4_out), ._3(I3_out), ._2(I2_out),
    ._1(I1_out), .ENTER(ENTER_out), .RESTART(RESTART_out));
  teclado teclado_1 (
    .out_12(teclado_1_out_12), .out_13(teclado_1_out_13), .out_14(teclado_1_out_14),
    .out_15(teclado_1_out_15), .out_16(teclado_1_out_16), .out_17(teclado_1_out_17),
    .out_18(teclado_1_out_18), .ENTER(ENTER_out), .RESTART(RESTART_out), .I2(I2_out), .I3(I3_out),
    .I4(I4_out), .I5(I5_out), .I6(I6_out), .I7(I7_out), .I8(I8_out), .I9(I9_out), .I1(I1_out));
  or or_1 (or_1_out, and_1_out, and_2_out, or_7_out, and_3_out, and_4_out);
  or or_2 (or_2_out, or_1_out, teclado_1_out_16, or_3_out, teclado_1_out_18);
  or or_3 (or_3_out, and_9_out, and_7_out, and_8_out);
  and and_1 (and_1_out, j_k_ff_5_q, or_4_out);
  or or_4 (or_4_out, ~j_k_ff_4_q, ~j_k_ff_3_q, ~j_k_ff_2_q, ~j_k_ff_1_q);  // OR_Gate
  and and_2 (and_2_out, j_k_ff_4_q, or_5_out);
  or or_5 (or_5_out, ~j_k_ff_3_q, ~j_k_ff_2_q, ~j_k_ff_1_q);  // OR_Gate
  and and_3 (and_3_out, ~j_k_ff_1_q, j_k_ff_2_q);  // AND_Gate
  and and_4 (and_4_out, j_k_ff_3_q, or_6_out);
  J_K_Flip_Flop j_k_ff_1 (
    .J(1'b1), .K(1'b1), .clk(teclado_1_out_12), .Q(j_k_ff_1_q), .reset(or_2_out));  // open: Qn, preset
  J_K_Flip_Flop j_k_ff_2 (
    .J(j_k_ff_1_q), .K(1'b1), .clk(teclado_1_out_13), .Q(j_k_ff_2_q), .reset(or_2_out));  // open: Qn, preset
  J_K_Flip_Flop j_k_ff_3 (
    .J(j_k_ff_2_q), .K(1'b1), .clk(teclado_1_out_14), .Q(j_k_ff_3_q), .reset(or_2_out));  // open: Qn, preset
  J_K_Flip_Flop j_k_ff_4 (
    .J(j_k_ff_3_q), .K(1'b1), .clk(teclado_1_out_15), .Q(j_k_ff_4_q), .reset(or_2_out));  // open: Qn, preset
  J_K_Flip_Flop j_k_ff_5 (
    .J(j_k_ff_4_q), .K(1'b1), .clk(teclado_1_out_17), .Q(j_k_ff_5_q), .reset(or_2_out));  // open: Qn, preset
  or or_6 (or_6_out, ~j_k_ff_2_q, ~j_k_ff_1_q);  // OR_Gate
  or or_7 (or_7_out, or_9_out, and_6_out);
  D_Flip_Flop d_ff_1 (.D(j_k_ff_1_q), .clk(j_k_ff_1_q), .Q(d_ff_1_q), .reset(and_6_out));  // open: Qn, preset
  and and_5 (and_5_out, j_k_ff_4_q, ~teclado_1_out_18, j_k_ff_5_q);  // AND_Gate
  and and_6 (and_6_out, d_ff_1_q, ~j_k_ff_1_q);  // AND_Gate
  and and_7 (and_7_out, ~j_k_ff_2_q, teclado_1_out_14);  // AND_Gate
  and and_8 (and_8_out, ~j_k_ff_3_q, teclado_1_out_15);  // AND_Gate
  LED led_1 (.in(and_5_out));
  and and_9 (and_9_out, ~j_k_ff_1_q, teclado_1_out_13);  // AND_Gate
  LED led_2 (.in(or_8_out));
  or or_8 (or_8_out, or_2_out, and_9_out, and_7_out, and_8_out);
  D_Flip_Flop d_ff_2 (.D(j_k_ff_2_q), .clk(j_k_ff_2_q), .Q(d_ff_2_q), .reset(and_10_out));  // open: Qn, preset
  D_Flip_Flop d_ff_3 (.D(j_k_ff_3_q), .clk(j_k_ff_3_q), .Q(d_ff_3_q), .reset(and_11_out));  // open: Qn, preset
  D_Flip_Flop d_ff_4 (.D(j_k_ff_4_q), .clk(j_k_ff_4_q), .Q(d_ff_4_q), .reset(and_12_out));  // open: Qn, preset
  and and_10 (and_10_out, d_ff_2_q, ~j_k_ff_2_q);  // AND_Gate
  or or_9 (or_9_out, and_10_out, and_11_out, and_12_out);
  and and_11 (and_11_out, d_ff_3_q, ~j_k_ff_3_q);  // AND_Gate
  and and_12 (and_12_out, d_ff_4_q, ~j_k_ff_4_q);  // AND_Gate

  // Notes on the sheet:
  //   9
  //   8
  //   7
  //   6
  //   5
  //   4
  //   3
  //   2
  //   1
  //   ENTER
  //   RESTART
endmodule

module teclado (
  input  I1,
  input  I2,
  input  I3,
  input  I4,
  input  I5,
  input  I6,
  input  I7,
  input  I8,
  input  I9,
  input  ENTER,
  input  RESTART,
  output out_12,
  output out_13,
  output out_14,
  output out_15,
  output out_16,
  output out_17,
  output out_18
);

  or or_1 (out_16, I6, I5, I2, I1, I8);

  assign out_12 = I9;
  assign out_13 = I3;
  assign out_14 = I7;
  assign out_15 = I4;
  assign out_17 = ENTER;
  assign out_18 = RESTART;
endmodule

module segredo (
  input  _9,
  input  _8,
  input  _7,
  input  _6,
  input  _5,
  input  _4,
  input  _3,
  input  _2,
  input  _1,
  input  ENTER,
  input  RESTART
);

  wire and_1_out, and_2_out, and_3_out, and_4_out, j_k_ff_1_q, j_k_ff_2_q, j_k_ff_3_q, j_k_ff_4_q,
       j_k_ff_5_q, or_1_out, or_2_out, or_3_out, teclado_1_out_12, teclado_1_out_13, teclado_1_out_14,
       teclado_1_out_15, teclado_1_out_16, teclado_1_out_17, teclado_1_out_18;

  teclado teclado_1 (
    .out_12(teclado_1_out_12), .out_13(teclado_1_out_13), .out_14(teclado_1_out_14),
    .out_15(teclado_1_out_15), .out_16(teclado_1_out_16), .out_17(teclado_1_out_17),
    .out_18(teclado_1_out_18), .ENTER(ENTER), .RESTART(RESTART), .I2(_2), .I3(_3), .I4(_4), .I5(_5), .I6(_6),
    .I7(_7), .I8(_8), .I9(_9), .I1(_1));
  or or_1 (or_1_out, teclado_1_out_16, teclado_1_out_18, or_2_out);
  or or_2 (or_2_out, and_2_out, and_3_out, and_4_out);
  J_K_Flip_Flop j_k_ff_1 (
    .J(1'b1), .K(1'b1), .clk(teclado_1_out_12), .Q(j_k_ff_1_q), .reset(or_1_out));  // open: Qn, preset
  J_K_Flip_Flop j_k_ff_2 (
    .J(j_k_ff_1_q), .K(1'b1), .clk(teclado_1_out_13), .Q(j_k_ff_2_q), .reset(or_1_out));  // open: Qn, preset
  J_K_Flip_Flop j_k_ff_3 (
    .J(j_k_ff_2_q), .K(1'b1), .clk(teclado_1_out_14), .Q(j_k_ff_3_q), .reset(or_1_out));  // open: Qn, preset
  J_K_Flip_Flop j_k_ff_4 (
    .J(j_k_ff_3_q), .K(1'b1), .clk(teclado_1_out_15), .Q(j_k_ff_4_q), .reset(or_1_out));  // open: Qn, preset
  J_K_Flip_Flop j_k_ff_5 (
    .J(j_k_ff_4_q), .K(1'b1), .clk(teclado_1_out_17), .Q(j_k_ff_5_q), .reset(or_1_out));  // open: Qn, preset
  and and_1 (and_1_out, j_k_ff_4_q, ~teclado_1_out_18, j_k_ff_5_q);  // AND_Gate
  LED led_1 (.in(and_1_out));
  and and_2 (and_2_out, ~j_k_ff_1_q, teclado_1_out_13);  // AND_Gate
  and and_3 (and_3_out, ~j_k_ff_2_q, teclado_1_out_14);  // AND_Gate
  and and_4 (and_4_out, ~j_k_ff_3_q, teclado_1_out_15);  // AND_Gate
  LED led_2 (.in(or_3_out));
  or or_3 (or_3_out, or_1_out, and_2_out, and_3_out, and_4_out);
endmodule

module segredo2 (
  input  _9,
  input  _8,
  input  _7,
  input  _6,
  input  _5,
  input  _4,
  input  _3,
  input  _2,
  input  _1,
  input  ENTER,
  input  RESTART
);

  wire and_1_out, and_2_out, and_3_out, and_4_out, and_5_out, and_6_out, and_7_out, and_8_out, and_9_out,
       and_10_out, and_11_out, and_12_out, d_ff_1_q, d_ff_2_q, d_ff_3_q, d_ff_4_q, j_k_ff_1_q, j_k_ff_2_q,
       j_k_ff_3_q, j_k_ff_4_q, j_k_ff_5_q, or_1_out, or_2_out, or_3_out, or_4_out, or_5_out, or_6_out,
       or_7_out, or_8_out, or_9_out, teclado_1_out_12, teclado_1_out_13, teclado_1_out_14, teclado_1_out_15,
       teclado_1_out_16, teclado_1_out_17, teclado_1_out_18;

  teclado teclado_1 (
    .out_12(teclado_1_out_12), .out_13(teclado_1_out_13), .out_14(teclado_1_out_14),
    .out_15(teclado_1_out_15), .out_16(teclado_1_out_16), .out_17(teclado_1_out_17),
    .out_18(teclado_1_out_18), .ENTER(ENTER), .RESTART(RESTART), .I2(_2), .I3(_3), .I4(_4), .I5(_5), .I6(_6),
    .I7(_7), .I8(_8), .I9(_9), .I1(_1));
  or or_1 (or_1_out, and_1_out, and_2_out, or_7_out, and_3_out, and_4_out);
  or or_2 (or_2_out, or_1_out, teclado_1_out_16, or_3_out, teclado_1_out_18);
  or or_3 (or_3_out, and_7_out, and_8_out, and_9_out);
  and and_1 (and_1_out, j_k_ff_5_q, or_4_out);
  or or_4 (or_4_out, ~j_k_ff_4_q, ~j_k_ff_3_q, ~j_k_ff_2_q, ~j_k_ff_1_q);  // OR_Gate
  and and_2 (and_2_out, j_k_ff_4_q, or_5_out);
  or or_5 (or_5_out, ~j_k_ff_3_q, ~j_k_ff_2_q, ~j_k_ff_1_q);  // OR_Gate
  and and_3 (and_3_out, ~j_k_ff_1_q, j_k_ff_2_q);  // AND_Gate
  and and_4 (and_4_out, j_k_ff_3_q, or_6_out);
  or or_6 (or_6_out, ~j_k_ff_2_q, ~j_k_ff_1_q);  // OR_Gate
  J_K_Flip_Flop j_k_ff_1 (
    .J(1'b1), .K(1'b1), .clk(teclado_1_out_12), .Q(j_k_ff_1_q), .reset(or_2_out));  // open: Qn, preset
  J_K_Flip_Flop j_k_ff_2 (
    .J(j_k_ff_1_q), .K(1'b1), .clk(teclado_1_out_13), .Q(j_k_ff_2_q), .reset(or_2_out));  // open: Qn, preset
  J_K_Flip_Flop j_k_ff_3 (
    .J(j_k_ff_2_q), .K(1'b1), .clk(teclado_1_out_14), .Q(j_k_ff_3_q), .reset(or_2_out));  // open: Qn, preset
  J_K_Flip_Flop j_k_ff_4 (
    .J(j_k_ff_3_q), .K(1'b1), .clk(teclado_1_out_15), .Q(j_k_ff_4_q), .reset(or_2_out));  // open: Qn, preset
  J_K_Flip_Flop j_k_ff_5 (
    .J(j_k_ff_4_q), .K(1'b1), .clk(teclado_1_out_17), .Q(j_k_ff_5_q), .reset(or_2_out));  // open: Qn, preset
  or or_7 (or_7_out, or_9_out, and_6_out);
  D_Flip_Flop d_ff_1 (.D(j_k_ff_1_q), .clk(j_k_ff_1_q), .Q(d_ff_1_q), .reset(and_6_out));  // open: Qn, preset
  and and_5 (and_5_out, j_k_ff_4_q, ~teclado_1_out_18, j_k_ff_5_q);  // AND_Gate
  LED led_1 (.in(and_5_out));
  and and_6 (and_6_out, d_ff_1_q, ~j_k_ff_1_q);  // AND_Gate
  and and_7 (and_7_out, ~j_k_ff_1_q, teclado_1_out_13);  // AND_Gate
  and and_8 (and_8_out, ~j_k_ff_2_q, teclado_1_out_14);  // AND_Gate
  and and_9 (and_9_out, ~j_k_ff_3_q, teclado_1_out_15);  // AND_Gate
  LED led_2 (.in(or_8_out));
  or or_8 (or_8_out, or_2_out, and_7_out, and_8_out, and_9_out);
  D_Flip_Flop d_ff_2 (.D(j_k_ff_2_q), .clk(j_k_ff_2_q), .Q(d_ff_2_q), .reset(and_10_out));  // open: Qn, preset
  D_Flip_Flop d_ff_3 (.D(j_k_ff_3_q), .clk(j_k_ff_3_q), .Q(d_ff_3_q), .reset(and_11_out));  // open: Qn, preset
  D_Flip_Flop d_ff_4 (.D(j_k_ff_4_q), .clk(j_k_ff_4_q), .Q(d_ff_4_q), .reset(and_12_out));  // open: Qn, preset
  or or_9 (or_9_out, and_10_out, and_11_out, and_12_out);
  and and_10 (and_10_out, d_ff_2_q, ~j_k_ff_2_q);  // AND_Gate
  and and_11 (and_11_out, d_ff_3_q, ~j_k_ff_3_q);  // AND_Gate
  and and_12 (and_12_out, d_ff_4_q, ~j_k_ff_4_q);  // AND_Gate
endmodule
