// Logisim project praticaContador1a18.circ as structural Verilog: 1 circuit, main circuit main
module main (
);

  wire and_1_out, and_2_out, clock_1_out, or_1_out;
  wire [3:0] t_ff_1_q, t_ff_2_q;

  Clock clock_1 (.out(clock_1_out));
  T_Flip_Flop #(.trigger("falling")) t_ff_1 (
    .T(1'b1), .clk(clock_1_out), .Q(t_ff_1_q[0]), .reset(or_1_out));  // open: Qn, preset
  T_Flip_Flop #(.trigger("falling")) t_ff_2 (
    .T(1'b1), .clk(t_ff_1_q[3]), .Q(t_ff_2_q[0]), .reset(and_2_out));  // open: Qn, preset
  T_Flip_Flop #(.trigger("falling")) t_ff_3 (
    .T(1'b1), .clk(t_ff_1_q[0]), .Q(t_ff_1_q[1]), .reset(or_1_out));  // open: Qn, preset
  T_Flip_Flop #(.trigger("falling")) t_ff_4 (
    .T(1'b1), .clk(t_ff_2_q[0]), .Q(t_ff_2_q[1]), .reset(and_2_out));  // open: Qn, preset
  T_Flip_Flop #(.trigger("falling")) t_ff_5 (
    .T(1'b1), .clk(t_ff_1_q[1]), .Q(t_ff_1_q[2]), .reset(or_1_out));  // open: Qn, preset
  T_Flip_Flop #(.trigger("falling")) t_ff_6 (
    .T(1'b1), .clk(t_ff_2_q[1]), .Q(t_ff_2_q[2]), .reset(and_2_out));  // open: Qn, preset
  T_Flip_Flop #(.trigger("falling")) t_ff_7 (
    .T(1'b1), .clk(t_ff_1_q[2]), .Q(t_ff_1_q[3]), .reset(or_1_out));  // open: Qn, preset
  or or_1 (or_1_out, and_1_out, and_2_out);
  T_Flip_Flop #(.trigger("falling")) t_ff_8 (
    .T(1'b1), .clk(t_ff_2_q[2]), .Q(t_ff_2_q[3]), .reset(and_2_out));  // open: Qn, preset
  and and_1 (and_1_out, t_ff_1_q[3], t_ff_1_q[0]);
  Hex_Digit_Display hex_digit_display_1 (.value(t_ff_2_q));  // open: dp
  and and_2 (and_2_out, t_ff_2_q[0], ~t_ff_2_q[3], ~t_ff_2_q[2], ~t_ff_2_q[1], and_1_out);  // AND_Gate
  Hex_Digit_Display hex_digit_display_2 (.value(t_ff_1_q));  // open: dp
endmodule
