// Logisim project praticaContadorDecrescente7ao3.circ as structural Verilog: 1 circuit, main circuit main
module main (
);

  wire and_1_out, clock_1_out;
  wire [2:0] t_ff_1_q;

  T_Flip_Flop t_ff_1 (.T(1'b1), .clk(clock_1_out), .Q(t_ff_1_q[0]), .reset(and_1_out));  // open: Qn, preset
  Clock clock_1 (.out(clock_1_out));
  T_Flip_Flop t_ff_2 (.T(1'b1), .clk(t_ff_1_q[0]), .Q(t_ff_1_q[1]), .reset(and_1_out));  // open: Qn, preset
  T_Flip_Flop t_ff_3 (.T(1'b1), .clk(t_ff_1_q[1]), .Q(t_ff_1_q[2]), .reset(and_1_out));  // open: Qn, preset
  and and_1 (and_1_out, ~t_ff_1_q[0], t_ff_1_q[1], ~t_ff_1_q[2]);  // AND_Gate
  Hex_Digit_Display hex_digit_display_1 (.value({1'b0, t_ff_1_q}));  // open: dp
endmodule
