// Logisim project praticaCronometro.circ as structural Verilog: 3 circuits, main circuit main
module main (
  input  in_1
);

  wire and_1_out, button_1_out, clock_1_out, cronometro_1_out_3, cronometro_2_2_out_3, cronometro_2_out_3;

  CRONOMETRO_2 cronometro_2_1 (.in_1(cronometro_1_out_3), .in_2(button_1_out));  // open: out_3
  CRONOMETRO cronometro_1 (.out_3(cronometro_1_out_3), .in_1(cronometro_2_2_out_3), .in_2(button_1_out));
  CRONOMETRO_2 cronometro_2_2 (.out_3(cronometro_2_2_out_3), .in_1(cronometro_2_out_3), .in_2(button_1_out));
  CRONOMETRO cronometro_2 (.out_3(cronometro_2_out_3), .in_1(and_1_out), .in_2(button_1_out));
  and and_1 (and_1_out, clock_1_out, in_1);
  Button button_1 (.out(button_1_out));
  Clock clock_1 (.out(clock_1_out));
endmodule

module CRONOMETRO (
  input  in_1,
  input  in_2,
  output out_3
);

  wire and_1_out, or_1_out;
  wire [2:0] t_ff_1_q;

  T_Flip_Flop #(.trigger("falling")) t_ff_1 (
    .T(1'b1), .clk(in_1), .Q(t_ff_1_q[0]), .reset(or_1_out));  // open: Qn, preset
  T_Flip_Flop #(.trigger("falling")) t_ff_2 (
    .T(1'b1), .clk(t_ff_1_q[0]), .Q(t_ff_1_q[1]), .reset(or_1_out));  // open: Qn, preset
  T_Flip_Flop #(.trigger("falling")) t_ff_3 (
    .T(1'b1), .clk(t_ff_1_q[1]), .Q(t_ff_1_q[2]), .reset(or_1_out));  // open: Qn, preset
  or or_1 (or_1_out, and_1_out, in_2);
  T_Flip_Flop #(.trigger("falling")) t_ff_4 (
    .T(1'b1), .clk(t_ff_1_q[2]), .Q(out_3), .reset(or_1_out));  // open: Qn, preset
  and and_1 (and_1_out, out_3, ~t_ff_1_q[2], t_ff_1_q[1], ~t_ff_1_q[0]);  // AND_Gate
  Hex_Digit_Display hex_digit_display_1 (.value({out_3, t_ff_1_q}));  // open: dp
endmodule

module CRONOMETRO_2 (
  input  in_1,
  input  in_2,
  output out_3
);

  wire and_1_out, or_1_out;
  wire [3:0] t_ff_1_q;

  T_Flip_Flop #(.trigger("falling")) t_ff_1 (
    .T(1'b1), .clk(in_1), .Q(t_ff_1_q[0]), .reset(or_1_out));  // open: Qn, preset
  T_Flip_Flop #(.trigger("falling")) t_ff_2 (
    .T(1'b1), .clk(t_ff_1_q[0]), .Q(t_ff_1_q[1]), .reset(or_1_out));  // open: Qn, preset
  T_Flip_Flop #(.trigger("falling")) t_ff_3 (
    .T(1'b1), .clk(t_ff_1_q[1]), .Q(out_3), .reset(or_1_out));  // open: Qn, preset
  or or_1 (or_1_out, and_1_out, in_2);
  T_Flip_Flop #(.trigger("falling")) t_ff_4 (
    .T(1'b1), .clk(out_3), .Q(t_ff_1_q[3]), .reset(or_1_out));  // open: Qn, preset
  and and_1 (and_1_out, ~t_ff_1_q[3], out_3, t_ff_1_q[1], ~t_ff_1_q[0]);  // AND_Gate
  Hex_Digit_Display hex_digit_display_1 (.value({t_ff_1_q[3], out_3, t_ff_1_q[1:0]}));  // open: dp
endmodule
