// Logisim project praticaRelogio.circ as structural Verilog: 3 circuits, main circuit main
module main (
);

  wire clock_1_out, relogio_1_out_3, relogio_2_out_3;

  relogio relogio_1 (.out_3(relogio_1_out_3), .in_2(relogio_2_out_3), .in_1(1'b1));
  relogio relogio_2 (.out_3(relogio_2_out_3), .in_2(clock_1_out), .in_1(1'b1));
  Clock clock_1 (.out(clock_1_out));
  HORA hora_1 (.in_1(1'b1), .in_2(relogio_1_out_3));  // open: out_3
endmodule

module relogio (
  input  in_1,
  input  in_2,
  output out_3
);

  wire and_2_out, and_3_out;
  wire [3:0] t_ff_1_q, t_ff_2_q;

  T_Flip_Flop #(.trigger("falling")) t_ff_1 (
    .T(in_1), .clk(in_2), .Q(t_ff_1_q[0]), .reset(and_3_out));  // open: Qn, preset
  T_Flip_Flop #(.trigger("falling")) t_ff_2 (
    .T(1'b1), .clk(t_ff_1_q[3]), .Q(t_ff_2_q[0]), .reset(and_2_out));  // open: Qn, preset
  T_Flip_Flop #(.trigger("falling")) t_ff_3 (
    .T(1'b1), .clk(t_ff_2_q[0]), .Q(t_ff_2_q[1]), .reset(and_2_out));  // open: Qn, preset
  T_Flip_Flop #(.trigger("falling")) t_ff_4 (
    .T(1'b1), .clk(t_ff_1_q[0]), .Q(t_ff_1_q[1]), .reset(and_3_out));  // open: Qn, preset
  T_Flip_Flop #(.trigger("falling")) t_ff_5 (
    .T(1'b1), .clk(t_ff_2_q[1]), .Q(t_ff_2_q[2]), .reset(and_2_out));  // open: Qn, preset
  T_Flip_Flop #(.trigger("falling")) t_ff_6 (
    .T(1'b1), .clk(t_ff_1_q[1]), .Q(t_ff_1_q[2]), .reset(and_3_out));  // open: Qn, preset
  and and_1 (out_3, t_ff_2_q[1], t_ff_2_q[2]);
  T_Flip_Flop #(.trigger("falling")) t_ff_7 (
    .T(1'b1), .clk(t_ff_1_q[2]), .Q(t_ff_1_q[3]), .reset(and_3_out));  // open: Qn, preset
  T_Flip_Flop #(.trigger("falling")) t_ff_8 (
    .T(1'b1), .clk(t_ff_2_q[2]), .Q(t_ff_2_q[3]), .reset(and_2_out));  // open: Qn, preset
  and and_2 (and_2_out, ~t_ff_2_q[3], t_ff_2_q[2], t_ff_2_q[1], ~t_ff_2_q[0]);  // AND_Gate
  and and_3 (and_3_out, t_ff_1_q[3], ~t_ff_1_q[2], t_ff_1_q[1], ~t_ff_1_q[0]);  // AND_Gate
  Hex_Digit_Display hex_digit_display_1 (.value(t_ff_2_q));  // open: dp
  Hex_Digit_Display hex_digit_display_2 (.value(t_ff_1_q));  // open: dp
endmodule

module HORA (
  input  in_1,
  input  in_2,
  output out_3
);

  wire and_1_out, and_3_out, and_4_out, and_5_out, and_6_out, and_7_out, button_1_out, button_2_out,
       multiplexer_1_out, multiplexer_2_out, or_1_out;
  wire [3:0] t_ff_1_q, t_ff_2_q;

  T_Flip_Flop #(.trigger("falling")) t_ff_1 (
    .T(1'b1), .clk(t_ff_2_q[3]), .Q(t_ff_1_q[0]), .reset(multiplexer_1_out));  // open: Qn, preset
  and and_1 (and_1_out, t_ff_1_q[1], and_4_out);
  T_Flip_Flop #(.trigger("falling")) t_ff_2 (
    .T(in_1), .clk(in_2), .Q(t_ff_2_q[0]), .reset(multiplexer_2_out));  // open: Qn, preset
  T_Flip_Flop #(.trigger("falling")) t_ff_3 (
    .T(1'b1), .clk(t_ff_1_q[0]), .Q(t_ff_1_q[1]), .reset(multiplexer_1_out));  // open: Qn, preset
  T_Flip_Flop #(.trigger("falling")) t_ff_4 (
    .T(1'b1), .clk(t_ff_2_q[0]), .Q(t_ff_2_q[1]), .reset(multiplexer_2_out));  // open: Qn, preset
  T_Flip_Flop #(.trigger("falling")) t_ff_5 (
    .T(1'b1), .clk(t_ff_1_q[1]), .Q(t_ff_1_q[2]), .reset(multiplexer_1_out));  // open: Qn, preset
  Multiplexer multiplexer_1 (.in0(and_1_out), .in1(and_3_out), .out(multiplexer_1_out), .sel(button_1_out));
  Button button_1 (.out(button_1_out));
  T_Flip_Flop #(.trigger("falling")) t_ff_6 (
    .T(1'b1), .clk(t_ff_2_q[1]), .Q(t_ff_2_q[2]), .reset(multiplexer_2_out));  // open: Qn, preset
  Multiplexer multiplexer_2 (.in0(or_1_out), .in1(and_7_out), .out(multiplexer_2_out), .sel(button_2_out));
  Button button_2 (.out(button_2_out));
  and and_2 (out_3, t_ff_1_q[1], t_ff_1_q[2]);
  T_Flip_Flop #(.trigger("falling")) t_ff_7 (
    .T(1'b1), .clk(t_ff_1_q[2]), .Q(t_ff_1_q[3]), .reset(multiplexer_1_out));  // open: Qn, preset
  T_Flip_Flop #(.trigger("falling")) t_ff_8 (
    .T(1'b1), .clk(t_ff_2_q[2]), .Q(t_ff_2_q[3]), .reset(multiplexer_2_out));  // open: Qn, preset
  and and_3 (and_3_out, ~t_ff_1_q[3], ~t_ff_1_q[2], t_ff_1_q[1], t_ff_1_q[0]);  // AND_Gate
  or or_1 (or_1_out, and_5_out, and_6_out);
  and and_4 (and_4_out, ~t_ff_2_q[0], ~t_ff_2_q[1], t_ff_2_q[2], ~t_ff_2_q[3]);  // AND_Gate
  and and_5 (and_5_out, and_4_out, and_7_out);
  and and_6 (and_6_out, t_ff_2_q[3], ~t_ff_2_q[2], t_ff_2_q[1], ~t_ff_2_q[0]);  // AND_Gate
  and and_7 (and_7_out, t_ff_2_q[2], t_ff_1_q[1]);
  Hex_Digit_Display hex_digit_display_1 (.value(t_ff_1_q));  // open: dp
  Hex_Digit_Display hex_digit_display_2 (.value(t_ff_2_q));  // open: dp
endmodule
