// Logisim project praticaSemafaro.circ as structural Verilog: 2 circuits, main circuit main
module main (
);

  wire button_1_out, clock_1_out;

  Clock clock_1 (.out(clock_1_out));
  semafaro semafaro_1 (.in_1(clock_1_out), .in_2(button_1_out));  // open: out_3
  Button button_1 (.out(button_1_out));
endmodule

module semafaro (
  input  in_1,
  input  in_2,
  output out_3
);

  wire and_1_out, and_2_out, and_3_out, and_4_out, and_5_out, and_6_out, and_7_out, and_8_out, and_9_out,
       and_10_out, and_11_out, and_12_out, and_13_out, or_1_out, or_2_out, or_3_out, or_4_out;
  wire [3:0] t_ff_1_q;

  T_Flip_Flop #(.trigger("falling")) t_ff_1 (
    .T(1'b1), .clk(in_1), .Q(t_ff_1_q[0]), .reset(or_1_out));  // open: Qn, preset
  T_Flip_Flop #(.trigger("falling")) t_ff_2 (
    .T(1'b1), .clk(t_ff_1_q[0]), .Q(t_ff_1_q[1]), .reset(or_1_out));  // open: Qn, preset
  T_Flip_Flop #(.trigger("falling")) t_ff_3 (
    .T(1'b1), .clk(t_ff_1_q[1]), .Q(out_3), .reset(or_1_out));  // open: Qn, preset
  or or_1 (or_1_out, and_1_out, in_2);
  T_Flip_Flop #(.trigger("falling")) t_ff_4 (
    .T(1'b1), .clk(out_3), .Q(t_ff_1_q[3]), .reset(or_1_out));  // open: Qn, preset
  and and_1 (and_1_out, t_ff_1_q[3], out_3, ~t_ff_1_q[1], ~t_ff_1_q[0]);  // AND_Gate
  Hex_Digit_Display hex_digit_display_1 (.value({t_ff_1_q[3], out_3, t_ff_1_q[1:0]}));  // open: dp
  and and_2 (and_2_out, t_ff_1_q[0], ~t_ff_1_q[1], ~out_3, ~t_ff_1_q[3]);  // AND_Gate
  and and_3 (and_3_out, ~t_ff_1_q[0], t_ff_1_q[1], ~out_3, ~t_ff_1_q[3]);  // AND_Gate
  and and_4 (and_4_out, t_ff_1_q[0], t_ff_1_q[1], ~out_3, ~t_ff_1_q[3]);  // AND_Gate
  and and_5 (and_5_out, ~t_ff_1_q[0], ~t_ff_1_q[1], out_3, ~t_ff_1_q[3]);  // AND_Gate
  and and_6 (and_6_out, t_ff_1_q[0], ~t_ff_1_q[1], out_3, ~t_ff_1_q[3]);  // AND_Gate
  and and_7 (and_7_out, ~t_ff_1_q[0], t_ff_1_q[1], out_3, ~t_ff_1_q[3]);  // AND_Gate
  and and_8 (and_8_out, t_ff_1_q[0], t_ff_1_q[1], out_3, ~t_ff_1_q[3]);  // AND_Gate
  and and_9 (and_9_out, ~t_ff_1_q[0], ~t_ff_1_q[1], ~out_3, t_ff_1_q[3]);  // AND_Gate
  and and_10 (and_10_out, t_ff_1_q[0], ~t_ff_1_q[1], ~out_3, t_ff_1_q[3]);  // AND_Gate
  and and_11 (and_11_out, ~t_ff_1_q[0], t_ff_1_q[1], ~out_3, t_ff_1_q[3]);  // AND_Gate
  and and_12 (and_12_out, t_ff_1_q[0], t_ff_1_q[1], ~out_3, t_ff_1_q[3]);  // AND_Gate
  and and_13 (and_13_out, ~t_ff_1_q[0], ~t_ff_1_q[1], out_3, t_ff_1_q[3]);  // AND_Gate
  or or_2 (or_2_out, and_2_out, and_3_out, and_4_out, and_5_out, and_6_out, and_7_out);
  or or_3 (or_3_out, and_8_out, and_9_out);
  or or_4 (or_4_out, and_10_out, and_11_out, and_12_out, and_13_out);
  LED led_1 (.in(or_2_out));
  LED led_2 (.in(or_3_out));
  LED led_3 (.in(or_4_out));
endmodule
