// Logisim project prsticaLogisinSomador.circ as structural Verilog: 2 circuits, main circuit main
module main (
  input  [3:0] A,
  input  [3:0] B,
  output COUT,
  output [3:0] S
);

  wire somador_1_cout, somador_2_cout, somador_3_cout;

  Somador somador_1 (.Cout(somador_1_cout), .S(S[0]), .A(A[0]), .B(B[0]), .Cin(1'b0));
  Somador somador_2 (.Cout(somador_2_cout), .S(S[2]), .A(A[1]), .B(B[1]), .Cin(somador_1_cout));
  Somador somador_3 (.Cout(somador_3_cout), .S(S[1]), .A(A[2]), .B(B[2]), .Cin(somador_2_cout));
  Somador somador_4 (.Cout(COUT), .S(S[3]), .A(A[3]), .B(B[3]), .Cin(somador_3_cout));
endmodule

module Somador (
  input  A,
  input  B,
  input  Cin,
  output Cout,
  output S
);

  wire and_1_out, and_2_out, and_3_out, xor_1_out;

  and and_1 (and_1_out, A, B);
  and and_2 (and_2_out, A, Cin);
  and and_3 (and_3_out, B, Cin);
  xor xor_1 (xor_1_out, A, B);
  xor xor_2 (S, xor_1_out, Cin);
  or or_1 (Cout, and_1_out, and_2_out, and_3_out);
endmodule
