// Logisim project simulacaoLogisin.circ as structural Verilog: 1 circuit, main circuit main
module main (
  input  A,
  input  C,
  input  B,
  input  D,
  output S
);

  wire or_1_out;

  or or_1 (or_1_out, A, C);
  and and_1 (S, or_1_out, ~B, ~D);  // AND_Gate
endmodule
