// Logisim project simulacaoLogisin02.circ as structural Verilog: 1 circuit, main circuit main
module main (
  input  X3,
  input  X2,
  input  X1,
  input  X0,
  output S
);

  wire and_1_out, and_2_out, and_3_out, and_4_out;

  and and_1 (and_1_out, X3, X2, X0);
  and and_2 (and_2_out, ~X0, ~X2, ~X3);  // AND_Gate
  and and_3 (and_3_out, ~X3, ~X2, ~X1);  // AND_Gate
  and and_4 (and_4_out, X1, X2, X3);
  or or_1 (S, and_1_out, and_2_out, and_3_out, and_4_out);
endmodule
